# Fritzing sketch overview_V2 (saved by Fritzing 0.9.3b)
breadboards: 1

parts:
  LED1 = RGB LED (com. cathode, rgb) [package="5 mm [THT]"]
  S1 = Pushbutton [package="[THT]"]
  R4 = Resistor [tolerance=±5% resistance=220 package=THT]
  R2 = Resistor [tolerance=±5% resistance=10k package=THT]
  R1 = Photocell (LDR) [package=THT]
  R5 = Resistor [tolerance=±5% resistance=220 package=THT]
  R6 = Resistor [tolerance=±5% resistance=220 package=THT]
  R7 = Resistor [tolerance=±1% resistance=5.1k package=THT]
  DS3231 = ZS-042 RTC Module
  R8 = Resistor [tolerance=±5% resistance=10k package=THT]
  R9 = Resistor [tolerance=±5% resistance=20k package=THT]
  Adafruit_HUZZAH_ESP8266_Breakout1 = Adafruit HUZZAH ESP8266 Breakout [part_number=2471]

nets (from the schematic view):
  N1: LED1.red_anode, R4.Pin_1
  GND: LED1.common_cathode, R2.Pin_1, R7.Pin_0, DS3231.GND, R8.Pin_0, Adafruit_HUZZAH_ESP8266_Breakout1.GND
  N2: LED1.green_anode, R6.Pin_0
  N3: LED1.blue_anode, R5.Pin_0
  N4: S1.Pin_1, S1.Pin_2, R2.Pin_0, Adafruit_HUZZAH_ESP8266_Breakout1.#16
  N5: S1.Pin_4, Adafruit_HUZZAH_ESP8266_Breakout1.3V
  N6: R4.Pin_0, Adafruit_HUZZAH_ESP8266_Breakout1.#14
  N7: R1.pin_0, R7.Pin_1, R9.Pin_1
  N8: R1.pin_1, R8.Pin_1, Adafruit_HUZZAH_ESP8266_Breakout1.A
  N9: R5.Pin_1, Adafruit_HUZZAH_ESP8266_Breakout1.#12
  N10: R6.Pin_1, Adafruit_HUZZAH_ESP8266_Breakout1.#13
  N11: DS3231.VCC, Adafruit_HUZZAH_ESP8266_Breakout1.V+
  N12: DS3231.SDA, Adafruit_HUZZAH_ESP8266_Breakout1.#4
  N13: DS3231.SCL, Adafruit_HUZZAH_ESP8266_Breakout1.#5
